// Logisim project 8BitAdder.circ as structural Verilog: 3 circuits, main circuit main
module main (
  input  CarryIn,
  input  A,
  input  B,
  input  A_2,
  input  in_5,
  input  in_6,
  input  in_7,
  input  in_8,
  input  in_9,
  input  in_10,
  input  in_11,
  input  in_12,
  input  in_13,
  input  in_14,
  input  in_15,
  input  in_16,
  input  in_17,
  input  B_2,
  input  in_19,
  output Sum,
  output CarryOut,
  output out_22,
  output out_23,
  output out_24,
  output out_25,
  output out_26,
  output out_27,
  output out_28,
  output out_29,
  output C
);

  wire and_1_out, and_2_out, fulladder_2_carryout, fulladder_3_carryout, fulladder_4_carryout,
       fulladder_5_carryout, fulladder_6_carryout, fulladder_7_carryout, fulladder_8_carryout, xor_1_out;

  FullAdder fulladder_1 (.CarryIn(fulladder_2_carryout), .A(A_2), .B(in_12), .Sum(out_23), .CarryOut(out_22));
  FullAdder fulladder_2 (
    .CarryIn(fulladder_3_carryout), .A(in_5), .B(in_13), .Sum(out_24), .CarryOut(fulladder_2_carryout));
  xor xor_1 (xor_1_out, A, B);
  and and_1 (and_1_out, A, B);
  FullAdder fulladder_3 (
    .CarryIn(fulladder_4_carryout), .A(in_6), .B(in_14), .Sum(out_25), .CarryOut(fulladder_3_carryout));
  xor xor_2 (Sum, CarryIn, xor_1_out);
  and and_2 (and_2_out, CarryIn, xor_1_out);
  or or_1 (CarryOut, and_2_out, and_1_out);
  FullAdder fulladder_4 (
    .CarryIn(fulladder_5_carryout), .A(in_7), .B(in_15), .Sum(out_26), .CarryOut(fulladder_4_carryout));
  FullAdder fulladder_5 (
    .CarryIn(fulladder_6_carryout), .A(in_8), .B(in_16), .Sum(out_27), .CarryOut(fulladder_5_carryout));
  FullAdder fulladder_6 (
    .CarryIn(fulladder_7_carryout), .A(in_9), .B(in_17), .Sum(out_28), .CarryOut(fulladder_6_carryout));
  FullAdder fulladder_7 (
    .CarryIn(fulladder_8_carryout), .A(in_10), .B(B_2), .Sum(out_29), .CarryOut(fulladder_7_carryout));
  FullAdder fulladder_8 (.A(in_11), .B(in_19), .Sum(C), .CarryOut(fulladder_8_carryout));  // open: CarryIn

  // Notes on the sheet:
  //   +
  //   +
  //   Overflow
  //   ⭡
endmodule

module HalfAdder (
  input  A,
  input  B,
  output Sum,
  output Carry
);

  and and_1 (Carry, A, B);
  xor xor_1 (Sum, A, B);

  // Notes on the sheet:
  //   +
  //   ⭡
endmodule

module FullAdder (
  input  CarryIn,
  input  A,
  input  B,
  output Sum,
  output CarryOut
);

  wire and_1_out, and_2_out, xor_1_out;

  xor xor_1 (xor_1_out, A, B);
  and and_1 (and_1_out, A, B);
  xor xor_2 (Sum, CarryIn, xor_1_out);
  and and_2 (and_2_out, CarryIn, xor_1_out);
  or or_1 (CarryOut, and_2_out, and_1_out);

  // Notes on the sheet:
  //   +
  //   +
  //   ⭡
endmodule
